// Logisim project CPU.circ as structural Verilog
module ALU (
  input  ZY,
  input  ZX,
  input  Nn,
  input  NX,
  input  F,
  input  NO,
  input  X1,
  input  X2,
  input  X3,
  input  X4,
  input  X5,
  input  X6,
  input  X7,
  input  X8,
  input  X9,
  input  X10,
  input  X11,
  input  X12,
  input  X13,
  input  X14,
  input  X15,
  input  X16,
  input  Y1,
  input  Y2,
  input  Y3,
  input  Y4,
  input  Y5,
  input  Y6,
  input  Y7,
  input  Y8,
  input  Y9,
  input  Y10,
  input  Y11,
  input  Y12,
  input  Y13,
  input  Y14,
  input  Y15,
  input  Y16,
  output R2,
  output R4,
  output R6,
  output R8,
  output R10,
  output R12,
  output R14,
  output R16,
  output R1,
  output R3,
  output R5,
  output R7,
  output R9,
  output R11,
  output R13,
  output R15,
  output negitve,
  output zero
);

  wire alu1bit_1_cout, alu1bit_2_cout, alu1bit_3_cout, alu1bit_4_cout, alu1bit_5_cout, alu1bit_6_cout,
       alu1bit_7_cout, alu1bit_8_cout, alu1bit_9_cout, alu1bit_10_cout, alu1bit_11_cout, alu1bit_12_cout,
       alu1bit_13_cout, alu1bit_14_cout, alu1bit_15_cout, or_1_out, or_2_out, or_3_out, or_4_out, or_5_out,
       or_6_out, or_7_out, or_8_out, or_9_out, or_10_out, or_11_out, or_12_out, or_13_out, or_14_out;

  ALU1Bit alu1bit_1 (
    .Cout(alu1bit_1_cout), .R1(R1), .NO(NO), .X(Y1), .Y(X1), .ZX(ZY), .ZY(ZX), .NX(Nn), .NY(NX), .F(F));  // open: CIN
  or or_1 (or_1_out, R1, R2);
  ALU1Bit alu1bit_2 (
    .Cout(alu1bit_2_cout), .R1(R2), .NO(NO), .X(Y2), .Y(X2), .ZX(ZY), .ZY(ZX), .NX(Nn), .NY(NX),
    .CIN(alu1bit_1_cout), .F(F));
  or or_2 (or_2_out, or_1_out, or_3_out);
  ALU1Bit alu1bit_3 (
    .Cout(alu1bit_3_cout), .R1(R3), .NO(NO), .X(Y3), .Y(X3), .ZX(ZY), .ZY(ZX), .NX(Nn), .NY(NX),
    .CIN(alu1bit_2_cout), .F(F));
  or or_3 (or_3_out, R3, R4);
  ALU1Bit alu1bit_4 (
    .Cout(alu1bit_4_cout), .R1(R4), .NO(NO), .X(Y4), .Y(X4), .ZX(ZY), .ZY(ZX), .NX(Nn), .NY(NX),
    .CIN(alu1bit_3_cout), .F(F));
  or or_4 (or_4_out, or_2_out, or_6_out);
  ALU1Bit alu1bit_5 (
    .Cout(alu1bit_5_cout), .R1(R5), .NO(NO), .X(Y5), .Y(X5), .ZX(ZY), .ZY(ZX), .NX(Nn), .NY(NX),
    .CIN(alu1bit_4_cout), .F(F));
  or or_5 (or_5_out, R5, R6);
  ALU1Bit alu1bit_6 (
    .Cout(alu1bit_6_cout), .R1(R6), .NO(NO), .X(Y6), .Y(X6), .ZX(ZY), .ZY(ZX), .NX(Nn), .NY(NX),
    .CIN(alu1bit_5_cout), .F(F));
  or or_6 (or_6_out, or_5_out, or_7_out);
  ALU1Bit alu1bit_7 (
    .Cout(alu1bit_7_cout), .R1(R7), .NO(NO), .X(Y7), .Y(X7), .ZX(ZY), .ZY(ZX), .NX(Nn), .NY(NX),
    .CIN(alu1bit_6_cout), .F(F));
  or or_7 (or_7_out, R7, R8);
  ALU1Bit alu1bit_8 (
    .Cout(alu1bit_8_cout), .R1(R8), .NO(NO), .X(Y8), .Y(X8), .ZX(ZY), .ZY(ZX), .NX(Nn), .NY(NX),
    .CIN(alu1bit_7_cout), .F(F));
  nor nor_1 (zero, or_4_out, or_11_out);
  ALU1Bit alu1bit_9 (
    .Cout(alu1bit_9_cout), .R1(R9), .NO(NO), .X(Y9), .Y(X9), .ZX(ZY), .ZY(ZX), .NX(Nn), .NY(NX),
    .CIN(alu1bit_8_cout), .F(F));
  or or_8 (or_8_out, R9, R10);
  ALU1Bit alu1bit_10 (
    .Cout(alu1bit_10_cout), .R1(R10), .NO(NO), .X(Y10), .Y(X10), .ZX(ZY), .ZY(ZX), .NX(Nn), .NY(NX),
    .CIN(alu1bit_9_cout), .F(F));
  or or_9 (or_9_out, or_8_out, or_10_out);
  ALU1Bit alu1bit_11 (
    .Cout(alu1bit_11_cout), .R1(R11), .NO(NO), .X(Y11), .Y(X11), .ZX(ZY), .ZY(ZX), .NX(Nn), .NY(NX),
    .CIN(alu1bit_10_cout), .F(F));
  or or_10 (or_10_out, R11, R12);
  ALU1Bit alu1bit_12 (
    .Cout(alu1bit_12_cout), .R1(R12), .NO(NO), .X(Y12), .Y(X12), .ZX(ZY), .ZY(ZX), .NX(Nn), .NY(NX),
    .CIN(alu1bit_11_cout), .F(F));
  or or_11 (or_11_out, or_9_out, or_13_out);
  ALU1Bit alu1bit_13 (
    .Cout(alu1bit_13_cout), .R1(R13), .NO(NO), .X(Y13), .Y(X13), .ZX(ZY), .ZY(ZX), .NX(Nn), .NY(NX),
    .CIN(alu1bit_12_cout), .F(F));
  or or_12 (or_12_out, R13, R14);
  ALU1Bit alu1bit_14 (
    .Cout(alu1bit_14_cout), .R1(R14), .NO(NO), .X(Y14), .Y(X14), .ZX(ZY), .ZY(ZX), .NX(Nn), .NY(NX),
    .CIN(alu1bit_13_cout), .F(F));
  or or_13 (or_13_out, or_12_out, or_14_out);
  ALU1Bit alu1bit_15 (
    .Cout(alu1bit_15_cout), .R1(negitve), .NO(NO), .X(Y15), .Y(X15), .ZX(ZY), .ZY(ZX), .NX(Nn), .NY(NX),
    .CIN(alu1bit_14_cout), .F(F));
  or or_14 (or_14_out, negitve, R16);
  ALU1Bit alu1bit_16 (
    .R1(R16), .NO(NO), .X(Y16), .Y(X16), .ZX(ZY), .ZY(ZX), .NX(Nn), .NY(NX), .CIN(alu1bit_15_cout), .F(F));  // open: Cout

  assign R15 = negitve;
endmodule

module halfAdder (
  input  in_1,
  input  in_2,
  output out_3,
  output out_4
);

  xor xor_1 (out_3, in_1, in_2);
  and and_1 (out_4, in_1, in_2);
endmodule

module adder (
  input  CIN,
  input  A1,
  input  B1,
  input  A2,
  input  B2,
  input  A3,
  input  B3,
  input  A4,
  input  B4,
  input  A5,
  input  B5,
  input  A6,
  input  B6,
  input  A7,
  input  B7,
  input  A8,
  input  B8,
  input  A9,
  input  B9,
  input  A10,
  input  B10,
  input  A11,
  input  B11,
  input  A12,
  input  B12,
  input  A13,
  input  B13,
  input  A14,
  input  B14,
  input  A15,
  input  B15,
  input  A16,
  input  B16,
  output R1,
  output R2,
  output R3,
  output R4,
  output R5,
  output R6,
  output R7,
  output R8,
  output R9,
  output R10,
  output R11,
  output R12,
  output R13,
  output R14,
  output R15,
  output R16,
  output COUT
);

  wire halfadder_1_out_3, halfadder_1_out_4, halfadder_2_out_3, halfadder_2_out_4, halfadder_3_out_3,
       halfadder_3_out_4, halfadder_4_out_3, halfadder_4_out_4, halfadder_5_out_3, halfadder_5_out_4,
       halfadder_6_out_3, halfadder_6_out_4, halfadder_7_out_4, halfadder_8_out_4, halfadder_9_out_4,
       halfadder_10_out_4, halfadder_11_out_4, halfadder_12_out_4, halfadder_13_out_3, halfadder_13_out_4,
       halfadder_14_out_4, halfadder_15_out_3, halfadder_15_out_4, halfadder_16_out_4, halfadder_17_out_3,
       halfadder_17_out_4, halfadder_18_out_3, halfadder_18_out_4, halfadder_19_out_3, halfadder_19_out_4,
       halfadder_20_out_3, halfadder_20_out_4, halfadder_21_out_3, halfadder_21_out_4, halfadder_22_out_3,
       halfadder_22_out_4, halfadder_23_out_3, halfadder_23_out_4, halfadder_24_out_3, halfadder_24_out_4,
       halfadder_25_out_4, halfadder_26_out_4, halfadder_27_out_4, halfadder_28_out_4, halfadder_29_out_4,
       halfadder_30_out_4, halfadder_31_out_4, halfadder_32_out_4, or_1_out, or_2_out, or_3_out, or_4_out,
       or_5_out, or_6_out, or_7_out, or_8_out, or_9_out, or_10_out, or_11_out, or_12_out, or_13_out,
       or_14_out, or_15_out;

  halfAdder halfadder_1 (.in_1(A1), .in_2(B1), .out_3(halfadder_1_out_3), .out_4(halfadder_1_out_4));
  halfAdder halfadder_2 (.in_1(A2), .in_2(B2), .out_3(halfadder_2_out_3), .out_4(halfadder_2_out_4));
  halfAdder halfadder_3 (.in_1(A3), .in_2(B3), .out_3(halfadder_3_out_3), .out_4(halfadder_3_out_4));
  halfAdder halfadder_4 (.in_1(A4), .in_2(B4), .out_3(halfadder_4_out_3), .out_4(halfadder_4_out_4));
  halfAdder halfadder_5 (.in_1(A5), .in_2(B5), .out_3(halfadder_5_out_3), .out_4(halfadder_5_out_4));
  halfAdder halfadder_6 (.in_1(A6), .in_2(B6), .out_3(halfadder_6_out_3), .out_4(halfadder_6_out_4));
  halfAdder halfadder_7 (.in_1(halfadder_1_out_3), .in_2(CIN), .out_3(R1), .out_4(halfadder_7_out_4));
  halfAdder halfadder_8 (.in_1(halfadder_2_out_3), .in_2(or_1_out), .out_3(R2), .out_4(halfadder_8_out_4));
  halfAdder halfadder_9 (.in_1(halfadder_3_out_3), .in_2(or_2_out), .out_3(R3), .out_4(halfadder_9_out_4));
  halfAdder halfadder_10 (.in_1(halfadder_4_out_3), .in_2(or_3_out), .out_3(R4), .out_4(halfadder_10_out_4));
  halfAdder halfadder_11 (.in_1(halfadder_5_out_3), .in_2(or_4_out), .out_3(R5), .out_4(halfadder_11_out_4));
  halfAdder halfadder_12 (.in_1(halfadder_6_out_3), .in_2(or_5_out), .out_3(R6), .out_4(halfadder_12_out_4));
  halfAdder halfadder_13 (.in_1(A7), .in_2(B7), .out_3(halfadder_13_out_3), .out_4(halfadder_13_out_4));
  halfAdder halfadder_14 (.in_1(halfadder_13_out_3), .in_2(or_6_out), .out_3(R7), .out_4(halfadder_14_out_4));
  halfAdder halfadder_15 (.in_1(A8), .in_2(B8), .out_3(halfadder_15_out_3), .out_4(halfadder_15_out_4));
  halfAdder halfadder_16 (.in_1(halfadder_15_out_3), .in_2(or_7_out), .out_3(R8), .out_4(halfadder_16_out_4));
  halfAdder halfadder_17 (.in_1(A9), .in_2(B9), .out_3(halfadder_17_out_3), .out_4(halfadder_17_out_4));
  halfAdder halfadder_18 (.in_1(A10), .in_2(B10), .out_3(halfadder_18_out_3), .out_4(halfadder_18_out_4));
  halfAdder halfadder_19 (.in_1(A11), .in_2(B11), .out_3(halfadder_19_out_3), .out_4(halfadder_19_out_4));
  halfAdder halfadder_20 (.in_1(A12), .in_2(B12), .out_3(halfadder_20_out_3), .out_4(halfadder_20_out_4));
  halfAdder halfadder_21 (.in_1(A13), .in_2(B13), .out_3(halfadder_21_out_3), .out_4(halfadder_21_out_4));
  halfAdder halfadder_22 (.in_1(A14), .in_2(B14), .out_3(halfadder_22_out_3), .out_4(halfadder_22_out_4));
  halfAdder halfadder_23 (.in_1(A15), .in_2(B15), .out_3(halfadder_23_out_3), .out_4(halfadder_23_out_4));
  halfAdder halfadder_24 (.in_1(A16), .in_2(B16), .out_3(halfadder_24_out_3), .out_4(halfadder_24_out_4));
  or or_1 (or_1_out, halfadder_7_out_4, halfadder_1_out_4);
  or or_2 (or_2_out, halfadder_8_out_4, halfadder_2_out_4);
  or or_3 (or_3_out, halfadder_9_out_4, halfadder_3_out_4);
  or or_4 (or_4_out, halfadder_10_out_4, halfadder_4_out_4);
  or or_5 (or_5_out, halfadder_11_out_4, halfadder_5_out_4);
  or or_6 (or_6_out, halfadder_12_out_4, halfadder_6_out_4);
  or or_7 (or_7_out, halfadder_14_out_4, halfadder_13_out_4);
  or or_8 (or_8_out, halfadder_16_out_4, halfadder_15_out_4);
  halfAdder halfadder_25 (.in_1(halfadder_17_out_3), .in_2(or_8_out), .out_3(R9), .out_4(halfadder_25_out_4));
  or or_9 (or_9_out, halfadder_25_out_4, halfadder_17_out_4);
  halfAdder halfadder_26 (.in_1(halfadder_18_out_3), .in_2(or_9_out), .out_3(R10), .out_4(halfadder_26_out_4));
  or or_10 (or_10_out, halfadder_26_out_4, halfadder_18_out_4);
  halfAdder halfadder_27 (.in_1(halfadder_19_out_3), .in_2(or_10_out), .out_3(R11), .out_4(halfadder_27_out_4));
  halfAdder halfadder_28 (.in_1(halfadder_20_out_3), .in_2(or_11_out), .out_3(R12), .out_4(halfadder_28_out_4));
  halfAdder halfadder_29 (.in_1(halfadder_21_out_3), .in_2(or_12_out), .out_3(R13), .out_4(halfadder_29_out_4));
  halfAdder halfadder_30 (.in_1(halfadder_22_out_3), .in_2(or_13_out), .out_3(R14), .out_4(halfadder_30_out_4));
  halfAdder halfadder_31 (.in_1(halfadder_23_out_3), .in_2(or_14_out), .out_3(R15), .out_4(halfadder_31_out_4));
  halfAdder halfadder_32 (.in_1(halfadder_24_out_3), .in_2(or_15_out), .out_3(R16), .out_4(halfadder_32_out_4));
  or or_11 (or_11_out, halfadder_27_out_4, halfadder_19_out_4);
  or or_12 (or_12_out, halfadder_28_out_4, halfadder_20_out_4);
  or or_13 (or_13_out, halfadder_29_out_4, halfadder_21_out_4);
  or or_14 (or_14_out, halfadder_30_out_4, halfadder_22_out_4);
  or or_15 (or_15_out, halfadder_31_out_4, halfadder_23_out_4);
  or or_16 (COUT, halfadder_32_out_4, halfadder_24_out_4);
endmodule

module incer (
  input  A1,
  input  in_2,
  input  A2,
  input  A3,
  input  A4,
  input  A5,
  input  A6,
  input  A74,
  input  A8,
  input  in_10,
  input  A9,
  input  in_12,
  input  A10,
  input  in_14,
  input  A11,
  input  in_16,
  input  A12,
  input  in_18,
  input  A13,
  input  in_20,
  input  A14,
  input  in_22,
  input  A15,
  input  in_24,
  input  A16,
  input  in_26,
  output R1,
  output R2,
  output R3,
  output R4,
  output R5,
  output R6,
  output R7,
  output R8,
  output R9,
  output R10,
  output R11,
  output R12,
  output R13,
  output R14,
  output R15,
  output R16,
  output Overflow
);

  adder adder_1 (
    .A1(A1), .B1(1'b1), .A2(A2), .B2(1'b0), .A3(A3), .B3(1'b0), .A4(A4), .B4(1'b0), .A5(A5), .B5(1'b0),
    .A6(A6), .B6(1'b0), .A7(A74), .B7(1'b0), .A8(A8), .B8(1'b0), .A9(A9), .B9(1'b0), .A10(A10), .B10(1'b0),
    .A11(A11), .B11(1'b0), .A12(A12), .B12(1'b0), .A13(A13), .B13(1'b0), .A14(A14), .B14(1'b0), .A15(A15),
    .B15(1'b0), .A16(A16), .B16(1'b0), .CIN(in_2), .R1(R1), .R2(R2), .R3(R3), .R4(R4), .R5(R5), .R6(R6),
    .R7(R7), .R8(R8), .R9(R9), .R10(R10), .R11(R11), .R12(R12), .R13(R13), .R14(R14), .R15(R15), .R16(R16),
    .COUT(Overflow));

  assign in_10 = A8;
  assign in_18 = A12;
  assign in_20 = A13;
  // also tied to GND on the sheet: {A3, A5, A9, A11, A15, A74, A13}
  // also tied to VCC on the sheet: A1
endmodule

module ALU1Bit (
  input  CIN,
  input  F,
  input  NO,
  input  ZX,
  input  ZY,
  input  NX,
  input  X,
  input  NY,
  input  Y,
  output R1,
  output Cout
);

  wire and_1_out, and_2_out, and_3_out, controlled_buffer_1_out, halfadder_1_out_3, halfadder_1_out_4,
       halfadder_2_out_3, halfadder_2_out_4, not_1_out, not_2_out, not_3_out, xor_1_out, xor_2_out;

  not not_1 (not_1_out, ZY);
  not not_2 (not_2_out, ZX);
  and and_1 (and_1_out, not_2_out, X);
  and and_2 (and_2_out, Y, not_1_out);
  xor xor_1 (xor_1_out, NX, and_1_out);
  xor xor_2 (xor_2_out, NY, and_2_out);
  halfAdder halfadder_1 (.in_1(xor_1_out), .in_2(xor_2_out), .out_3(halfadder_1_out_3), .out_4(halfadder_1_out_4));
  halfAdder halfadder_2 (.in_1(halfadder_1_out_3), .in_2(CIN), .out_3(halfadder_2_out_3), .out_4(halfadder_2_out_4));
  assign controlled_buffer_1_out = F ? halfadder_2_out_3 : 1'bz;  // Controlled_Buffer controlled_buffer_1
  or or_1 (Cout, halfadder_2_out_4, halfadder_1_out_4);
  and and_3 (and_3_out, xor_1_out, xor_2_out);
  assign controlled_buffer_1_out = not_3_out ? and_3_out : 1'bz;  // Controlled_Buffer controlled_buffer_2
  not not_3 (not_3_out, F);
  xor xor_3 (R1, NO, controlled_buffer_1_out);
endmodule

module Register1bit (
  input  load,
  input  data,
  output out_3
);

  wire and_1_out, and_2_out, nor_1_out, not_1_out;

  not not_1 (not_1_out, data);
  and and_1 (and_1_out, data, load);
  and and_2 (and_2_out, not_1_out, load);
  nor nor_1 (nor_1_out, and_1_out, out_3);
  nor nor_2 (out_3, nor_1_out, and_2_out);
endmodule

module Register16bit (
  input  load,
  input  [15:0] data,
  output [15:0] out_3
);

  wire [15:0] and_1_out, and_2_out, bit_extender_1_out, nor_1_out, not_1_out;

  assign bit_extender_1_out = {{15{load}}, load};  // Bit_Extender bit_extender_1
  assign and_1_out = data & bit_extender_1_out;  // AND_Gate and_1, 16 bits wide
  assign not_1_out = ~data;  // NOT_Gate not_1, 16 bits wide
  assign and_2_out = not_1_out & bit_extender_1_out;  // AND_Gate and_2, 16 bits wide
  assign nor_1_out = ~(and_1_out | out_3);  // NOR_Gate nor_1, 16 bits wide
  assign out_3 = ~(nor_1_out | and_2_out);  // NOR_Gate nor_2, 16 bits wide
endmodule

module ram8 (
  input  [15:0] val,
  input  load,
  input  [2:0] address,
  input  reset,
  output [15:0] value
);

  wire demultiplexer_1_out0, demultiplexer_1_out1, demultiplexer_1_out2, demultiplexer_1_out3,
       demultiplexer_1_out4, demultiplexer_1_out5, demultiplexer_1_out6, demultiplexer_1_out7;
  wire [15:0] resetigster_1_out_4, resetigster_2_out_4, resetigster_3_out_4, resetigster_4_out_4,
       resetigster_5_out_4, resetigster_6_out_4, resetigster_7_out_4, resetigster_8_out_4;

  Demultiplexer #(.select(3)) demultiplexer_1 (
    .out0(demultiplexer_1_out0), .out1(demultiplexer_1_out1), .out2(demultiplexer_1_out2),
    .out3(demultiplexer_1_out3), .out4(demultiplexer_1_out4), .out5(demultiplexer_1_out5),
    .out6(demultiplexer_1_out6), .out7(demultiplexer_1_out7), .in(load), .sel(address));
  resetigster resetigster_1 (.load(demultiplexer_1_out0), .data(val), .reset(reset), .out_4(resetigster_1_out_4));
  resetigster resetigster_2 (.load(demultiplexer_1_out1), .data(val), .reset(reset), .out_4(resetigster_2_out_4));
  resetigster resetigster_3 (.load(demultiplexer_1_out2), .data(val), .reset(reset), .out_4(resetigster_3_out_4));
  resetigster resetigster_4 (.load(demultiplexer_1_out3), .data(val), .reset(reset), .out_4(resetigster_4_out_4));
  resetigster resetigster_5 (.load(demultiplexer_1_out4), .data(val), .reset(reset), .out_4(resetigster_5_out_4));
  resetigster resetigster_6 (.load(demultiplexer_1_out5), .data(val), .reset(reset), .out_4(resetigster_6_out_4));
  resetigster resetigster_7 (.load(demultiplexer_1_out6), .data(val), .reset(reset), .out_4(resetigster_7_out_4));
  resetigster resetigster_8 (.load(demultiplexer_1_out7), .data(val), .reset(reset), .out_4(resetigster_8_out_4));
  Multiplexer #(.select(3), .width(16)) multiplexer_1 (
    .in0(resetigster_1_out_4), .in1(resetigster_2_out_4), .in2(resetigster_3_out_4),
    .in3(resetigster_4_out_4), .in4(resetigster_5_out_4), .in5(resetigster_6_out_4),
    .in6(resetigster_7_out_4), .in7(resetigster_8_out_4), .out(value), .sel(address));
endmodule

module ram64 (
  input  [15:0] val,
  input  load,
  input  clk,
  input  [5:0] in_4,
  input  reset,
  output [15:0] out_6
);

  wire and_1_out, demultiplexer_1_out0, demultiplexer_1_out1, demultiplexer_1_out2, demultiplexer_1_out3,
       demultiplexer_1_out4, demultiplexer_1_out5, demultiplexer_1_out6, demultiplexer_1_out7;
  wire [15:0] ram8_1_value, ram8_2_value, ram8_3_value, ram8_4_value, ram8_5_value, ram8_6_value,
       ram8_7_value, ram8_8_value;

  and and_1 (and_1_out, load, clk);
  Demultiplexer #(.select(3)) demultiplexer_1 (
    .out0(demultiplexer_1_out0), .out1(demultiplexer_1_out1), .out2(demultiplexer_1_out2),
    .out3(demultiplexer_1_out3), .out4(demultiplexer_1_out4), .out5(demultiplexer_1_out5),
    .out6(demultiplexer_1_out6), .out7(demultiplexer_1_out7), .in(and_1_out), .sel(in_4[2:0]));
  ram8 ram8_1 (.val(val), .load(demultiplexer_1_out0), .address(in_4[5:3]), .reset(reset), .value(ram8_1_value));
  ram8 ram8_2 (.val(val), .load(demultiplexer_1_out1), .address(in_4[5:3]), .reset(reset), .value(ram8_2_value));
  ram8 ram8_3 (.val(val), .load(demultiplexer_1_out2), .address(in_4[5:3]), .reset(reset), .value(ram8_3_value));
  ram8 ram8_4 (.val(val), .load(demultiplexer_1_out3), .address(in_4[5:3]), .reset(reset), .value(ram8_4_value));
  ram8 ram8_5 (.val(val), .load(demultiplexer_1_out4), .address(in_4[5:3]), .reset(reset), .value(ram8_5_value));
  ram8 ram8_6 (.val(val), .load(demultiplexer_1_out5), .address(in_4[5:3]), .reset(reset), .value(ram8_6_value));
  ram8 ram8_7 (.val(val), .load(demultiplexer_1_out6), .address(in_4[5:3]), .reset(reset), .value(ram8_7_value));
  ram8 ram8_8 (.val(val), .load(demultiplexer_1_out7), .address(in_4[5:3]), .reset(reset), .value(ram8_8_value));
  Multiplexer #(.select(3), .width(16)) multiplexer_1 (
    .in0(ram8_1_value), .in1(ram8_2_value), .in2(ram8_3_value), .in3(ram8_4_value), .in4(ram8_5_value),
    .in5(ram8_6_value), .in6(ram8_7_value), .in7(ram8_8_value), .out(out_6), .sel(in_4[2:0]));
endmodule

module ram512 (
  input  [15:0] val,
  input  load,
  input  [8:0] in_3,
  output [15:0] out_4
);

  wire demultiplexer_1_out0, demultiplexer_1_out1, demultiplexer_1_out2, demultiplexer_1_out3,
       demultiplexer_1_out4, demultiplexer_1_out5, demultiplexer_1_out6, demultiplexer_1_out7;
  wire [3:0] undriven, undriven_2, undriven_3, undriven_4;
  wire [15:0] ram64_1_p5, ram64_2_p4, ram64_3_p5, ram64_4_p4, ram64_5_p5, ram64_6_p4, ram64_7_p5, ram64_8_p4;

  Demultiplexer #(.select(3)) demultiplexer_1 (
    .out0(demultiplexer_1_out0), .out1(demultiplexer_1_out1), .out2(demultiplexer_1_out2),
    .out3(demultiplexer_1_out3), .out4(demultiplexer_1_out4), .out5(demultiplexer_1_out5),
    .out6(demultiplexer_1_out6), .out7(demultiplexer_1_out7), .in(load), .sel(in_3[2:0]));
  // ram64 ram64_1: pin names not known; wires that end beside it: val, demultiplexer_1_out0, in_3[8:3], val, ram64_1_p5
  // ram64 ram64_2: pin names not known; wires that end beside it: val, demultiplexer_1_out1, in_3[8:3], ram64_2_p4
  // ram64 ram64_3: pin names not known; wires that end beside it: val, demultiplexer_1_out2, in_3[8:3], val, ram64_3_p5
  // ram64 ram64_4: pin names not known; wires that end beside it: val, demultiplexer_1_out3, in_3[8:3], ram64_4_p4
  // ram64 ram64_5: pin names not known; wires that end beside it: val, demultiplexer_1_out4, in_3[8:3], val, ram64_5_p5
  // ram64 ram64_6: pin names not known; wires that end beside it: val, demultiplexer_1_out5, in_3[8:3], ram64_6_p4
  // ram64 ram64_7: pin names not known; wires that end beside it: val, demultiplexer_1_out6, in_3[8:3], val, ram64_7_p5
  // ram64 ram64_8: pin names not known; wires that end beside it: val, demultiplexer_1_out7, in_3[8:3], ram64_8_p4
  Multiplexer #(.select(3), .width(16)) multiplexer_1 (
    .in0(ram64_1_p5), .in1(ram64_2_p4), .in2(ram64_3_p5), .in3(ram64_4_p4), .in4(ram64_5_p5),
    .in5(ram64_6_p4), .in6(ram64_7_p5), .in7(ram64_8_p4), .out(out_4), .sel(in_3[2:0]));
  Hex_Digit_Display hex_digit_display_1 (.value(undriven_4));  // open: dp
  Hex_Digit_Display hex_digit_display_2 (.value(undriven_3));  // open: dp
  Hex_Digit_Display hex_digit_display_3 (.value(undriven_2));  // open: dp
  Hex_Digit_Display hex_digit_display_4 (.value(undriven));  // open: dp
endmodule

module ram4k (
  input  [15:0] val,
  input  load,
  input  [11:0] in_3,
  output [15:0] out_4
);

  wire demultiplexer_1_out0, demultiplexer_1_out1, demultiplexer_1_out2, demultiplexer_1_out3,
       demultiplexer_1_out4, demultiplexer_1_out5, demultiplexer_1_out6, demultiplexer_1_out7;
  wire [15:0] ram512_1_out_4, ram512_2_out_4, ram512_3_out_4, ram512_4_p4, ram512_5_out_4, ram512_6_out_4,
       ram512_7_out_4, ram512_8_out_4;

  Demultiplexer #(.select(3)) demultiplexer_1 (
    .out0(demultiplexer_1_out0), .out1(demultiplexer_1_out1), .out2(demultiplexer_1_out2),
    .out3(demultiplexer_1_out3), .out4(demultiplexer_1_out4), .out5(demultiplexer_1_out5),
    .out6(demultiplexer_1_out6), .out7(demultiplexer_1_out7), .in(load), .sel(in_3[2:0]));
  ram512 ram512_1 (.val(val), .load(demultiplexer_1_out0), .in_3(in_3[11:3]), .out_4(ram512_1_out_4));
  ram512 ram512_2 (.val(val), .load(demultiplexer_1_out1), .in_3(in_3[11:3]), .out_4(ram512_2_out_4));
  ram512 ram512_3 (.val(val), .load(demultiplexer_1_out2), .in_3(in_3[11:3]), .out_4(ram512_3_out_4));
  // ram512 ram512_4: pin names not known; wires that end beside it: val, demultiplexer_1_out3, in_3[11:3], ram512_4_p4
  ram512 ram512_5 (.val(val), .load(demultiplexer_1_out4), .in_3(in_3[11:3]), .out_4(ram512_5_out_4));
  ram512 ram512_6 (.val(val), .load(demultiplexer_1_out5), .in_3(in_3[11:3]), .out_4(ram512_6_out_4));
  ram512 ram512_7 (.val(val), .load(demultiplexer_1_out6), .in_3(in_3[11:3]), .out_4(ram512_7_out_4));
  ram512 ram512_8 (.val(val), .load(demultiplexer_1_out7), .in_3(in_3[11:3]), .out_4(ram512_8_out_4));
  Multiplexer #(.select(3), .width(16)) multiplexer_1 (
    .in0(ram512_1_out_4), .in1(ram512_2_out_4), .in2(ram512_3_out_4), .in3(ram512_4_p4),
    .in4(ram512_5_out_4), .in5(ram512_6_out_4), .in6(ram512_7_out_4), .in7(ram512_8_out_4), .out(out_4),
    .sel(in_3[2:0]));
endmodule

module pc (
  input  load,
  input  [15:0] num,
  input  reset,
  input  clk,
  output [15:0] val
);

  wire not_1_out, not_2_out, not_3_out;
  wire [15:0] adder_1_out, controlled_buffer_1_out, controlled_buffer_3_out, register16bit_1_out_3;

  not not_1 (not_1_out, reset);
  not not_2 (not_2_out, load);
  assign controlled_buffer_1_out = load ? num : 16'bz;  // Controlled_Buffer controlled_buffer_1
  assign controlled_buffer_1_out = not_2_out ? adder_1_out : 16'bz;  // Controlled_Buffer controlled_buffer_2
  assign controlled_buffer_3_out = not_1_out ? controlled_buffer_1_out : 16'bz;  // Controlled_Buffer controlled_buffer_3
  not not_3 (not_3_out, clk);
  Register16bit register16bit_1 (.load(clk), .data(controlled_buffer_3_out), .out_3(register16bit_1_out_3));
  Adder #(.width(16)) adder_1 (.a(val), .b(16'h1), .out(adder_1_out));  // open: cin, cout
  Register16bit register16bit_2 (.load(not_3_out), .data(register16bit_1_out_3), .out_3(val));
endmodule

module halfadder16 (
  input  [15:0] in_1,
  input  [15:0] in_2,
  output [15:0] out_3,
  output [15:0] out_4
);

  assign out_3 = in_1 ^ in_2;  // XOR_Gate xor_1, 16 bits wide
  assign out_4 = in_1 & in_2;  // AND_Gate and_1, 16 bits wide
endmodule

module JKflipflop (
  input  in_1,
  input  in_2,
  output out_3,
  output out_4
);

  wire clock_1_out, nand_1_out, nand_2_out, nand_3_out, nand_4_out, nand_5_out, nand_6_out, not_1_out;

  Clock clock_1 (.out(clock_1_out));
  nand nand_1 (nand_1_out, out_4, in_1, clock_1_out);
  nand nand_2 (nand_2_out, clock_1_out, in_2, out_3);
  nand nand_3 (nand_3_out, nand_1_out, nand_4_out);
  nand nand_4 (nand_4_out, nand_3_out, nand_2_out);
  not not_1 (not_1_out, clock_1_out);
  nand nand_5 (nand_5_out, nand_3_out, not_1_out);
  nand nand_6 (nand_6_out, not_1_out, nand_4_out);
  nand nand_7 (out_3, nand_5_out, out_4);
  nand nand_8 (out_4, out_3, nand_6_out);
endmodule

module hack (
  input  reset,
  input  in_2,
  input  [15:0] in_3,
  input  [15:0] in_4,
  input  in_5,
  output [15:0] out_6,
  output [15:0] out_7,
  output [15:0] out_8,
  output [15:0] out_9,
  output [7:0] out_10,
  output [7:0] out_11,
  output [14:0] out_12,
  output [15:0] out_13,
  output [15:0] out_14,
  output [15:0] out_15,
  output [14:0] dataout
);

  wire and_1_out, clock_1_out, cpu_1_writem, not_1_out, or_1_out, or_2_out, or_3_out, rgb_video_1_p1;
  wire [15:0] controlled_buffer_1_out, rom_1_data;

  ROM #(.addrWidth(16), .dataWidth(16)) rom_1 (.addr(out_14), .data(rom_1_data));
  Clock clock_1 (.out(clock_1_out));
  Register16bit register16bit_1 (.load(or_1_out), .data(out_6), .out_3(out_8));
  or or_1 (or_1_out, reset, not_1_out);
  Register16bit register16bit_2 (.load(or_2_out), .data(out_7), .out_3(out_6));
  cpu cpu_1 (
    .instruction(rom_1_data), .reset(reset), .inM(out_8), .clk(clock_1_out), .outM(out_9), .addressM(out_13),
    .pcOut(out_14), .writeM(cpu_1_writem));
  dataMem datamem_1 (
    .load(in_2), .value(in_4), .addr(in_3), .clk(in_5), .reset(in_5), .val(out_15));  // open: x, y, data
  not not_1 (not_1_out, clock_1_out);
  or or_2 (or_2_out, reset, clock_1_out);
  assign controlled_buffer_1_out = cpu_1_writem ? out_9 : 16'bz;  // Controlled_Buffer controlled_buffer_1
  or or_3 (or_3_out, cpu_1_writem, reset, reset);
  and and_1 (and_1_out, or_3_out, clock_1_out);
  dataMem datamem_2 (
    .load(and_1_out), .value(controlled_buffer_1_out), .addr(out_13), .clk(clock_1_out), .reset(reset),
    .val(out_7), .x(out_10), .y(out_11), .data(out_12));
  // RGB_Video #(.height(256), .width(256)) rgb_video_1: pin names not known; wires that end beside it: rgb_video_1_p1, rgb_video_1_p1, clock_1_out, 1'b1, out_10, out_11, out_12

  // Notes on the sheet:
  //   contents of rom_1 (hex, n*v repeats v):
  //   40 fdc8 c0 fdc8 0 efc7
endmodule

module cpu (
  input  [15:0] instruction,
  input  reset,
  input  [15:0] inM,
  input  clk,
  output [15:0] outM,
  output [15:0] addressM,
  output [15:0] pcOut,
  output writeM
);

  wire alu_1_negitve, alu_1_zero, and_1_out, and_2_out, and_3_out, and_4_out, nor_1_out, not_1_out,
       not_2_out, or_1_out, or_2_out, or_3_out;
  wire [15:0] alu_1_r1, controlled_buffer_1_out, multiplexer_1_out, multiplexer_2_out, register16bit_2_out_3;

  Multiplexer #(.width(16)) multiplexer_1 (.in0(alu_1_r1), .in1(instruction), .out(multiplexer_1_out), .sel(not_1_out));
  or or_1 (or_1_out, instruction[5], not_1_out);
  not not_1 (not_1_out, instruction[15]);
  or or_2 (or_2_out, reset, instruction[4]);
  Register16bit register16bit_1 (.load(or_1_out), .data(multiplexer_1_out), .out_3(addressM));
  assign controlled_buffer_1_out = instruction[15] ? instruction : 16'bz;  // Controlled_Buffer controlled_buffer_1
  Multiplexer #(.width(16)) multiplexer_2 (.in0(addressM), .in1(inM), .out(multiplexer_2_out), .sel(instruction[12]));
  Register16bit register16bit_2 (.load(or_2_out), .data(alu_1_r1), .out_3(register16bit_2_out_3));
  or or_3 (or_3_out, and_2_out, and_3_out, and_4_out);
  and and_1 (and_1_out, or_3_out, instruction[15]);
  and and_2 (and_2_out, instruction[2], alu_1_negitve);
  ALU alu_1 (
    .ZY(controlled_buffer_1_out[9]), .ZX(controlled_buffer_1_out[11]), .Nn(controlled_buffer_1_out[8]),
    .NX(controlled_buffer_1_out[10]), .F(controlled_buffer_1_out[7]), .NO(controlled_buffer_1_out[6]),
    .X1(register16bit_2_out_3[0]), .X2(register16bit_2_out_3[1]), .X3(register16bit_2_out_3[2]),
    .X4(register16bit_2_out_3[3]), .X5(register16bit_2_out_3[4]), .X6(register16bit_2_out_3[5]),
    .X7(register16bit_2_out_3[6]), .X8(register16bit_2_out_3[7]), .X9(register16bit_2_out_3[8]),
    .X10(register16bit_2_out_3[9]), .X11(register16bit_2_out_3[10]), .X12(register16bit_2_out_3[11]),
    .X13(register16bit_2_out_3[12]), .X14(register16bit_2_out_3[13]), .X15(register16bit_2_out_3[14]),
    .X16(register16bit_2_out_3[15]), .Y1(multiplexer_2_out[0]), .Y2(multiplexer_2_out[1]),
    .Y3(multiplexer_2_out[2]), .Y4(multiplexer_2_out[3]), .Y5(multiplexer_2_out[4]),
    .Y6(multiplexer_2_out[5]), .Y7(multiplexer_2_out[6]), .Y8(multiplexer_2_out[7]),
    .Y9(multiplexer_2_out[8]), .Y10(multiplexer_2_out[9]), .Y11(multiplexer_2_out[10]),
    .Y12(multiplexer_2_out[11]), .Y13(multiplexer_2_out[12]), .Y14(multiplexer_2_out[13]),
    .Y15(multiplexer_2_out[14]), .Y16(multiplexer_2_out[15]), .R2(alu_1_r1[1]), .R4(alu_1_r1[4]),
    .R6(alu_1_r1[5]), .R8(alu_1_r1[7]), .R10(alu_1_r1[9]), .R12(alu_1_r1[11]), .R14(alu_1_r1[13]),
    .R16(alu_1_r1[15]), .R1(alu_1_r1[0]), .R3(alu_1_r1[2]), .R5(alu_1_r1[3]), .R7(alu_1_r1[6]),
    .R9(alu_1_r1[8]), .R11(alu_1_r1[10]), .R13(alu_1_r1[12]), .R15(alu_1_r1[14]), .negitve(alu_1_negitve),
    .zero(alu_1_zero));
  and and_3 (and_3_out, instruction[1], alu_1_zero);
  pc pc_1 (.load(and_1_out), .num(addressM), .reset(reset), .clk(clk), .val(pcOut));
  nor nor_1 (nor_1_out, alu_1_zero, alu_1_negitve);
  and and_4 (and_4_out, instruction[0], nor_1_out);
  not not_2 (not_2_out, clk);
  Multiplexer #(.width(16)) multiplexer_3 (.in0(inM), .in1(alu_1_r1), .out(outM), .sel(instruction[3]));

  assign writeM = instruction[3];
endmodule

module dataMem (
  input  load,
  input  [15:0] value,
  input  [15:0] addr,
  input  clk,
  input  reset,
  output [15:0] val,
  output [7:0] x,
  output [7:0] y,
  output [14:0] data
);

  wire and_1_out, or_1_out;
  wire [5:0] bit_extender_1_out;
  wire [15:0] ram64_1_out_6, viddriver_1_out16bit;

  Bit_Extender #(.in_width(16), .out_width(6)) bit_extender_1 (.in(addr), .out(bit_extender_1_out));
  or or_1 (or_1_out, addr[6], addr[7]);
  and and_1 (and_1_out, load, or_1_out);
  ram64 ram64_1 (.val(value), .load(load), .clk(clk), .in_4(bit_extender_1_out), .reset(reset), .out_6(ram64_1_out_6));
  vidDriver viddriver_1 (
    .load(and_1_out), .addr(addr[7:6]), .dataIn(value), .reset(reset), .out16bit(viddriver_1_out16bit),
    .xout(x), .yout(y), .dataout(data));
  Multiplexer #(.width(16)) multiplexer_1 (.in0(ram64_1_out_6), .in1(viddriver_1_out16bit), .out(val), .sel(or_1_out));
endmodule

module ram16k (
);

  ram4k ram4k_1 ();  // open: val, load, in_3, out_4
  ram4k ram4k_2 ();  // open: val, load, in_3, out_4
  ram4k ram4k_3 ();  // open: val, load, in_3, out_4
  ram4k ram4k_4 ();  // open: val, load, in_3, out_4
endmodule

module rom32 (
  input  [14:0] addr,
  output instruction
);
endmodule

module resetigster (
  input  load,
  input  [15:0] data,
  input  reset,
  output [15:0] out_4
);

  wire not_1_out, or_1_out;
  wire [15:0] and_1_out, and_2_out, bit_extender_1_out, bit_extender_2_out, multiplexer_1_out, nor_1_out,
       not_2_out;

  not not_1 (not_1_out, reset);
  or or_1 (or_1_out, load, reset);
  Multiplexer #(.width(16)) multiplexer_1 (.in0(data), .in1(bit_extender_1_out), .out(multiplexer_1_out), .sel(reset));
  assign bit_extender_1_out = {{15{not_1_out}}, not_1_out};  // Bit_Extender bit_extender_1
  assign bit_extender_2_out = {{15{or_1_out}}, or_1_out};  // Bit_Extender bit_extender_2
  assign and_1_out = multiplexer_1_out & bit_extender_2_out;  // AND_Gate and_1, 16 bits wide
  assign not_2_out = ~multiplexer_1_out;  // NOT_Gate not_2, 16 bits wide
  assign and_2_out = not_2_out & bit_extender_2_out;  // AND_Gate and_2, 16 bits wide
  assign nor_1_out = ~(and_1_out | out_4);  // NOR_Gate nor_1, 16 bits wide
  assign out_4 = ~(nor_1_out | and_2_out);  // NOR_Gate nor_2, 16 bits wide
endmodule

module vidDriver (
  input  load,
  input  [1:0] addr,
  input  [15:0] dataIn,
  input  reset,
  output [15:0] out16bit,
  output [7:0] xout,
  output [7:0] yout,
  output [14:0] dataout
);

  wire demultiplexer_1_out1, demultiplexer_1_out2, demultiplexer_1_out3;
  wire [15:0] data_out_4, x_out_4, y_out_4;

  Demultiplexer #(.select(2)) demultiplexer_1 (
    .out1(demultiplexer_1_out1), .out2(demultiplexer_1_out2), .out3(demultiplexer_1_out3), .in(load),
    .sel(addr));  // open: out0
  resetigster x (.load(demultiplexer_1_out3), .data(dataIn), .reset(reset), .out_4(x_out_4));
  resetigster y (.load(demultiplexer_1_out1), .data(dataIn), .reset(reset), .out_4(y_out_4));
  resetigster data (.load(demultiplexer_1_out2), .data(dataIn), .reset(reset), .out_4(data_out_4));
  Bit_Extender #(.in_width(16), .out_width(15)) bit_extender_1 (.in(data_out_4), .out(dataout));
  Multiplexer #(.select(2), .width(16)) multiplexer_1 (
    .in1(y_out_4), .in2(data_out_4), .in3(x_out_4), .out(out16bit), .sel(addr));  // open: in0
  Bit_Extender #(.in_width(16), .out_width(8)) bit_extender_2 (.in(x_out_4), .out(xout));
  Bit_Extender #(.in_width(16), .out_width(8)) bit_extender_3 (.in(y_out_4), .out(yout));
endmodule

// VHDL entity ram16, as the project stores it:
--------------------------------------------------------------------------------
-- Project :
-- File    :
-- Autor   :
-- Date    :
--
--------------------------------------------------------------------------------
-- Description :
--
--------------------------------------------------------------------------------

LIBRARY ieee;
USE ieee.std_logic_1164.all;

ENTITY ram16 IS
  PORT (
  ------------------------------------------------------------------------------
  --Insert input ports below
    clock      : IN  std_logic;                    -- input bit example
    val        : IN  std_logic_vector(3 DOWNTO 0); -- input vector example
  ------------------------------------------------------------------------------
  --Insert output ports below
    max        : OUT std_logic;                    -- output bit example
    cpt        : OUT std_logic_vector(3 DOWNTO 0)  -- output vector example
    );
END ram16;

--------------------------------------------------------------------------------
--Complete your VHDL description below
--------------------------------------------------------------------------------

ARCHITECTURE TypeArchitecture OF ram16 IS

BEGIN


END TypeArchitecture;
